# Fritzing sketch BB-8-v1-Electronics (saved by Fritzing 0.9.2b)
breadboards: 1

parts:
  Part1 = Arduino Mega 2560 (Rev3)
  GY2 = MPU-6050 Board GY-521 [form="♀ (female)" package=THT]
  MD03A1 = Dual VNH2SP30 Motor Driver [part_number=MD03A]
  M1 = DC Motor
  M2 = DC Motor
  M3 = DC Motor
  VCC1 = LC-R121R3P
  U1 = Voltage Regulator - 5V [package="TO220 [THT]"]
  Part2 = Bluetooth Mate Silver

nets:
  N1: Part1.A0, MD03A1.1CS
  N2: Part1.A1, MD03A1.2CS
  N3: Part1.D21/SCL, GY2.pin3
  N4: Part1.D20/SDA, GY2.pin4
  N5: Part1.D13_PWM, Part2.RTS_5V, Part2.RX_5V
  N6: Part1.D12_PWM, MD03A1.2DIAG/EN
  N7: Part1.D11_PWM, Part2.TX_5V
  N8: Part1.D10_PWM, MD03A1.2PWM
  N9: Part1.D9_PWM, MD03A1.PWM
  N10: Part1.D8_PWM, MD03A1.2INb#143
  N11: Part1.D2_PWM, GY2.pin8
  N12: Part1.D3_PWM, MD03A1.1INa
  N13: Part1.D4_PWM, MD03A1.1INb
  N14: Part1.D6_PWM, MD03A1.1DIAG/EN
  N15: Part1.D7_PWM, MD03A1.2INb#142
  N16: GY2.pin1, U1.output_voltage, Part2.VCC, Part2.CTS_5V
  N17: GY2.pin2, Part2.GND
  N18: MD03A1.OUT_1A, M2.pin_1, M3.pin_2
  N19: MD03A1.OUT_1B, M2.pin_2, M3.pin_1
  N20: MD03A1.OUT_2A, M1.pin_1
  N21: MD03A1.OUT_2B, M1.pin_2
  N22: MD03A1.VIN, VCC1.pin1, U1.input_voltage
  GND: MD03A1.GND, VCC1.pin2, U1.GND

notes:
  Pololu shield mappings (I use VNH5019, not the VNH2SP30 as shown here.)
  VOUT -> 12V to ARDins
  M1EN/DIAG -> Arduino D6
  M1INA -> Arduino D3 (remapped from D2)
  M1INB -> Arduino D4
  M1PWM -> Arduino D9
  M1CS -> Arduino A0
  M2EN/DIAG -> Arduino D12
  M2INA -> Arduino D7
  M2INB -> Arduino D8
  M2PWM -> Arduino D10
  M2CS -> Arduino A1

custom parts:
  MPU-6050 Board GY-521: Acelerometro y Giroscopio MPU-6050 Board GY-521
  LC-R121R3P: 12V 1.Ah battery
